// Logisim project ALU.circ as structural Verilog: 11 circuits, main circuit 74181
module _74181 (
  input  [3:0] F,
  input  [3:0] B,
  input  [3:0] A,
  input  M,
  input  C,
  output Y,
  output C_2,
  output X,
  output [3:0] Out,
  output Eq
);

  wire and_1_out, and_2_out, and_3_out, and_4_out, and_5_out, and_6_out, and_7_out, and_8_out, and_9_out,
       and_10_out, and_11_out, and_12_out, and_13_out, and_14_out, and_15_out, and_16_out, and_17_out,
       and_18_out, and_19_out, and_20_out, and_21_out, and_22_out, and_23_out, and_24_out, and_25_out,
       and_26_out, and_27_out, and_28_out, nand_1_out, nand_3_out, nor_1_out, nor_2_out, nor_3_out,
       nor_4_out, nor_5_out, nor_6_out, nor_7_out, nor_8_out, nor_9_out, nor_10_out, nor_11_out, not_1_out,
       not_2_out, not_3_out, not_4_out, not_5_out, not_6_out, or_1_out, xor_1_out, xor_2_out, xor_3_out,
       xor_4_out;

  not not_1 (not_1_out, B[3]);
  not not_2 (not_2_out, B[2]);
  not not_3 (not_3_out, B[1]);
  not not_4 (not_4_out, B[0]);
  not not_5 (not_5_out, M);
  not not_6 (not_6_out, C);
  and and_1 (and_1_out, B[3], F[3], A[3]);
  and and_2 (and_2_out, A[3], F[2], not_1_out);
  and and_3 (and_3_out, not_1_out, F[1]);
  and and_4 (and_4_out, F[0], B[3]);
  and and_5 (and_5_out, B[2], F[3], A[2]);
  and and_6 (and_6_out, A[2], F[2], not_2_out);
  and and_7 (and_7_out, not_2_out, F[1]);
  and and_8 (and_8_out, F[0], B[2]);
  and and_9 (and_9_out, B[1], F[3], A[1]);
  and and_10 (and_10_out, A[1], F[2], not_3_out);
  and and_11 (and_11_out, not_3_out, F[1]);
  and and_12 (and_12_out, F[0], B[1]);
  and and_13 (and_13_out, B[0], F[3], A[0]);
  and and_14 (and_14_out, A[0], F[2], not_4_out);
  and and_15 (and_15_out, not_4_out, F[1]);
  and and_16 (and_16_out, F[0], B[0]);
  nor nor_1 (nor_1_out, and_1_out, and_2_out);
  nor nor_2 (nor_2_out, and_3_out, and_4_out, A[3]);
  nor nor_3 (nor_3_out, and_5_out, and_6_out);
  nor nor_4 (nor_4_out, and_7_out, and_8_out, A[2]);
  nor nor_5 (nor_5_out, and_9_out, and_10_out);
  nor nor_6 (nor_6_out, and_11_out, and_12_out, A[1]);
  nor nor_7 (nor_7_out, and_13_out, and_14_out);
  nor nor_8 (nor_8_out, and_15_out, and_16_out, A[0]);
  xor xor_1 (xor_1_out, nor_5_out, nor_6_out);
  xor xor_2 (xor_2_out, nor_7_out, nor_8_out);
  xor xor_3 (xor_3_out, nor_1_out, nor_2_out);
  xor xor_4 (xor_4_out, nor_3_out, nor_4_out);
  and and_17 (and_17_out, nor_1_out, nor_4_out);
  and and_18 (and_18_out, nor_1_out, nor_3_out, nor_6_out);
  and and_19 (and_19_out, nor_1_out, nor_3_out, nor_5_out, nor_8_out);
  nand nand_1 (nand_1_out, nor_1_out, nor_3_out, nor_5_out, nor_7_out, not_6_out);
  not nand_2 (X, nor_7_out);  // NAND_Gate
  and and_20 (and_20_out, not_6_out, nor_7_out, nor_5_out, nor_3_out, not_5_out);
  and and_21 (and_21_out, nor_5_out, nor_3_out, nor_8_out, not_5_out);
  and and_22 (and_22_out, nor_3_out, nor_6_out, not_5_out);
  and and_23 (and_23_out, nor_4_out, not_5_out);
  and and_24 (and_24_out, not_6_out, nor_7_out, nor_5_out, not_5_out);
  and and_25 (and_25_out, nor_5_out, nor_8_out, not_5_out);
  and and_26 (and_26_out, nor_6_out, not_5_out);
  and and_27 (and_27_out, not_6_out, nor_7_out, not_5_out);
  and and_28 (and_28_out, nor_8_out, not_5_out);
  nand nand_3 (nand_3_out, not_6_out, not_5_out);
  nor nor_9 (nor_9_out, and_20_out, and_21_out, and_22_out, and_23_out);
  nor nor_10 (nor_10_out, and_24_out, and_25_out, and_26_out);
  nor nor_11 (nor_11_out, and_27_out, and_28_out);
  nor nor_12 (Y, nor_2_out, and_17_out, and_18_out, and_19_out);
  xor xor_5 (Out[3], xor_3_out, nor_9_out);
  xor xor_6 (Out[2], xor_4_out, nor_10_out);
  xor xor_7 (Out[1], xor_1_out, nor_11_out);
  not not_7 (C_2, or_1_out);
  or or_1 (or_1_out, ~Y, ~nand_1_out);  // OR_Gate
  xor xor_8 (Out[0], xor_2_out, nand_3_out);
  and and_29 (Eq, Out[3], Out[2], Out[1], Out[0]);
endmodule

module ALU (
  input  [3:0] in_1,
  input  [7:0] in_2,
  input  [7:0] in_3,
  input  in_4,
  input  in_5,
  output [7:0] out_6,
  output out_7,
  output out_8
);

  wire n74181_1_c_2, n74181_1_eq, n74181_2_eq;

  _74181 u_74181_1 (
    .B(in_3[3:0]), .A(in_2[3:0]), .M(in_4), .C(in_5), .C_2(n74181_1_c_2), .Out(out_6[3:0]), .Eq(n74181_1_eq),
    .F(in_1));  // open: Y, X
  _74181 u_74181_2 (
    .B(in_3[7:4]), .A(in_2[7:4]), .M(in_4), .C(n74181_1_c_2), .C_2(out_7), .Out(out_6[7:4]),
    .Eq(n74181_2_eq), .F(in_1));  // open: Y, X
  and and_1 (out_8, n74181_1_eq, n74181_2_eq);
endmodule

module Logic_Unit (
  input  in_1,
  input  in_2,
  input  in_3,
  input  in_4,
  input  in_5,
  output out_6,
  output out_7,
  output out_8
);

  wire and_1_out, not_1_out, or_1_out;

  and and_1 (and_1_out, in_1, in_2);
  or or_1 (or_1_out, in_1, in_2);
  not not_1 (not_1_out, in_2);
  and and_2 (out_6, and_1_out, in_3);
  and and_3 (out_7, or_1_out, in_4);
  and and_4 (out_8, not_1_out, in_5);
endmodule

module Basic_ALU_Cell (
  input  Carry_In,
  input  INVA,
  input  A,
  input  ENA,
  input  B,
  input  ENB,
  input  F0,
  input  F1,
  output Output,
  output Carry_Out
);

  wire and_1_out, and_2_out, decoder_1_out_3, decoder_1_out_4, decoder_1_out_5, decoder_1_out_6,
       full_adder_1_out_5, logic_unit_1_out_6, logic_unit_1_out_7, logic_unit_1_out_8, xor_1_out;

  and and_1 (and_1_out, A, ENA);
  and and_2 (and_2_out, B, ENB);
  Decoder decoder_1 (
    .in_1(F0), .in_2(F1), .out_3(decoder_1_out_3), .out_4(decoder_1_out_4), .out_5(decoder_1_out_5),
    .out_6(decoder_1_out_6));
  xor xor_1 (xor_1_out, INVA, and_1_out);
  Logic_Unit logic_unit_1 (
    .in_1(xor_1_out), .in_2(and_2_out), .in_3(decoder_1_out_3), .in_4(decoder_1_out_4),
    .in_5(decoder_1_out_5), .out_6(logic_unit_1_out_6), .out_7(logic_unit_1_out_7), .out_8(logic_unit_1_out_8));
  Full_Adder full_adder_1 (
    .in_2(xor_1_out), .in_3(and_2_out), .in_4(decoder_1_out_6), .in_1(Carry_In), .out_6(Carry_Out),
    .out_5(full_adder_1_out_5));
  or or_1 (Output, logic_unit_1_out_6, logic_unit_1_out_7, logic_unit_1_out_8, full_adder_1_out_5);
endmodule

module Decoder (
  input  in_1,
  input  in_2,
  output out_3,
  output out_4,
  output out_5,
  output out_6
);

  and and_1 (out_3, ~in_1, ~in_2);  // AND_Gate
  and and_2 (out_4, ~in_1, in_2);  // AND_Gate
  and and_3 (out_5, in_1, ~in_2);  // AND_Gate
  and and_4 (out_6, in_1, in_2);
endmodule

module Full_Adder (
  input  in_1,
  input  in_2,
  input  in_3,
  input  in_4,
  output out_5,
  output out_6
);

  wire and_1_out, and_2_out, xor_1_out, xor_2_out;

  and and_1 (and_1_out, in_4, in_3, in_2);
  and and_2 (and_2_out, in_4, xor_1_out, in_1);
  or or_1 (out_6, and_1_out, and_2_out);
  xor xor_1 (xor_1_out, in_2, in_3);
  xor xor_2 (xor_2_out, in_1, xor_1_out);
  and and_3 (out_5, xor_2_out, in_4);
endmodule

module Basic_ALU_8b (
  input  [7:0] A,
  input  [7:0] B,
  input  [5:0] Control,
  output out_4,
  output [7:0] Output,
  output out_6
);

  wire basic_alu_cell_2_carry_out, basic_alu_cell_3_carry_out, basic_alu_cell_4_carry_out,
       basic_alu_cell_5_carry_out, basic_alu_cell_6_carry_out, basic_alu_cell_7_carry_out,
       basic_alu_cell_8_carry_out;

  Basic_ALU_Cell basic_alu_cell_1 (
    .INVA(Control[1]), .A(A[7]), .ENA(Control[3]), .B(B[7]), .ENB(Control[2]), .F0(Control[5]),
    .F1(Control[4]), .Output(Output[7]), .Carry_In(basic_alu_cell_2_carry_out), .Carry_Out(out_4));
  Basic_ALU_Cell basic_alu_cell_2 (
    .INVA(Control[1]), .A(A[6]), .ENA(Control[3]), .B(B[6]), .ENB(Control[2]), .F0(Control[5]),
    .F1(Control[4]), .Output(Output[6]), .Carry_In(basic_alu_cell_3_carry_out),
    .Carry_Out(basic_alu_cell_2_carry_out));
  Basic_ALU_Cell basic_alu_cell_3 (
    .INVA(Control[1]), .A(A[5]), .ENA(Control[3]), .B(B[5]), .ENB(Control[2]), .F0(Control[5]),
    .F1(Control[4]), .Output(Output[5]), .Carry_In(basic_alu_cell_4_carry_out),
    .Carry_Out(basic_alu_cell_3_carry_out));
  Basic_ALU_Cell basic_alu_cell_4 (
    .INVA(Control[1]), .A(A[4]), .ENA(Control[3]), .B(B[4]), .ENB(Control[2]), .F0(Control[5]),
    .F1(Control[4]), .Output(Output[4]), .Carry_In(basic_alu_cell_5_carry_out),
    .Carry_Out(basic_alu_cell_4_carry_out));
  nor nor_1 (out_6, Output[7], Output[6], Output[5], Output[4], Output[3], Output[2], Output[1], Output[0]);
  Basic_ALU_Cell basic_alu_cell_5 (
    .INVA(Control[1]), .A(A[3]), .ENA(Control[3]), .B(B[3]), .ENB(Control[2]), .F0(Control[5]),
    .F1(Control[4]), .Output(Output[3]), .Carry_In(basic_alu_cell_6_carry_out),
    .Carry_Out(basic_alu_cell_5_carry_out));
  Basic_ALU_Cell basic_alu_cell_6 (
    .INVA(Control[1]), .A(A[2]), .ENA(Control[3]), .B(B[2]), .ENB(Control[2]), .F0(Control[5]),
    .F1(Control[4]), .Output(Output[2]), .Carry_In(basic_alu_cell_7_carry_out),
    .Carry_Out(basic_alu_cell_6_carry_out));
  Basic_ALU_Cell basic_alu_cell_7 (
    .INVA(Control[1]), .A(A[1]), .ENA(Control[3]), .B(B[1]), .ENB(Control[2]), .F0(Control[5]),
    .F1(Control[4]), .Output(Output[1]), .Carry_In(basic_alu_cell_8_carry_out),
    .Carry_Out(basic_alu_cell_7_carry_out));
  Basic_ALU_Cell basic_alu_cell_8 (
    .INVA(Control[1]), .A(A[0]), .ENA(Control[3]), .B(B[0]), .ENB(Control[2]), .F0(Control[5]),
    .F1(Control[4]), .Output(Output[0]), .Carry_In(Control[0]), .Carry_Out(basic_alu_cell_8_carry_out));

  // Other names for the same wires on the sheet: INC = Control[0]; Control_t[2:0] = Control[3:1];
  //   F[1:0] = Control[5:4]
endmodule

module Shifter (
  input  [31:0] in_1,
  input  [1:0] in_2,
  input  Clk,
  output [31:0] out_4
);

  wire and_1_out;
  wire [1:0] controlled_buffer_1_out;

  assign controlled_buffer_1_out = Clk ? in_2 : 2'bz;  // Controlled_Buffer controlled_buffer_1
  Pull_Resistor pull_resistor_1 (.node(controlled_buffer_1_out));
  and and_1 (and_1_out, ~controlled_buffer_1_out[1], ~controlled_buffer_1_out[0]);  // AND_Gate
  assign out_4 = and_1_out ? in_1 : 32'bz;  // Controlled_Buffer controlled_buffer_2
  assign out_4 = controlled_buffer_1_out[1] ? {in_1[23:0], in_1[31:24]} : 32'bz;  // Controlled_Buffer controlled_buffer_3
  assign out_4 = controlled_buffer_1_out[0] ? {in_1[30:0], in_1[31]} : 32'bz;  // Controlled_Buffer controlled_buffer_4

  // Other names for the same wires on the sheet: ShifterControl[1:0] = in_2
endmodule

module Basic_ALU_32b (
  input  [31:0] A,
  input  [31:0] B,
  input  [5:0] Control,
  output out_4,
  output [31:0] Output,
  output [1:0] Flag_NZ
);

  wire basic_alu_8b_1_out_6, basic_alu_8b_2_out_6, basic_alu_8b_3_out_6, basic_alu_8b_4_out_6;
  wire [0:0] basic_alu_8b_2_out_4, basic_alu_8b_3_out_4, basic_alu_8b_4_out_4;

  Basic_ALU_8b basic_alu_8b_1 (
    .out_4(out_4), .Control({Control[5:1], basic_alu_8b_2_out_4[0]}), .A(A[31:24]), .B(B[31:24]),
    .Output({Flag_NZ[1], Output[30:24]}), .out_6(basic_alu_8b_1_out_6));
  Basic_ALU_8b basic_alu_8b_2 (
    .out_4(basic_alu_8b_2_out_4[0]), .Control({Control[5:1], basic_alu_8b_3_out_4[0]}), .A(A[23:16]),
    .B(B[23:16]), .Output(Output[23:16]), .out_6(basic_alu_8b_2_out_6));
  nor nor_1 (Flag_NZ[0], basic_alu_8b_1_out_6, basic_alu_8b_2_out_6, basic_alu_8b_3_out_6, basic_alu_8b_4_out_6);
  Basic_ALU_8b basic_alu_8b_3 (
    .out_4(basic_alu_8b_3_out_4[0]), .Control({Control[5:1], basic_alu_8b_4_out_4[0]}), .A(A[15:8]),
    .B(B[15:8]), .Output(Output[15:8]), .out_6(basic_alu_8b_3_out_6));
  Basic_ALU_8b basic_alu_8b_4 (
    .out_4(basic_alu_8b_4_out_4[0]), .Control(Control), .A(A[7:0]), .B(B[7:0]), .Output(Output[7:0]),
    .out_6(basic_alu_8b_4_out_6));

  assign Output[31] = Flag_NZ[1];

  // Other names for the same wires on the sheet: Flag[1:0] = Flag_NZ
endmodule

module Latch (
  input  [31:0] in_1,
  output [31:0] out_2
);

  wire [31:0] nand_1_out, not_1_out;

  Pull_Resistor pull_resistor_1 (.node(in_1));
  assign nand_1_out = ~(in_1 & out_2);  // NAND_Gate nand_1, 32 bits wide
  assign not_1_out = ~in_1;  // NOT_Gate not_1, 32 bits wide
  assign out_2 = ~(nand_1_out & not_1_out);  // NAND_Gate nand_2, 32 bits wide
endmodule

module ALU_x86 (
  input  [31:0] A,
  input  [31:0] B,
  input  [5:0] Control,
  output out_4,
  output [31:0] Output,
  output [1:0] Flag_NZ
);

  wire basic_alu_8b_1_out_6, basic_alu_8b_2_out_6, basic_alu_8b_3_out_6, basic_alu_8b_4_out_6, or_1_out;
  wire [0:0] basic_alu_8b_2_out_4, basic_alu_8b_3_out_4, basic_alu_8b_4_out_4;
  wire [6:0] basic_alu_8b_1_output;
  wire [7:0] basic_alu_8b_2_output;
  wire [15:0] basic_alu_8b_4_output;

  Basic_ALU_8b basic_alu_8b_1 (
    .out_4(out_4), .Control({Control[5:1], basic_alu_8b_2_out_4[0]}), .A(A[31:24]), .B(B[31:24]),
    .Output({Flag_NZ[1], basic_alu_8b_1_output}), .out_6(basic_alu_8b_1_out_6));
  Basic_ALU_8b basic_alu_8b_2 (
    .out_4(basic_alu_8b_2_out_4[0]), .Control({Control[5:1], basic_alu_8b_3_out_4[0]}), .A(A[23:16]),
    .B(B[23:16]), .Output(basic_alu_8b_2_output), .out_6(basic_alu_8b_2_out_6));
  assign Output = or_1_out ? {Flag_NZ[1], basic_alu_8b_1_output, basic_alu_8b_2_output, basic_alu_8b_4_output} : 32'bz;  // Controlled_Buffer controlled_buffer_1
  nor nor_1 (Flag_NZ[0], basic_alu_8b_1_out_6, basic_alu_8b_2_out_6, basic_alu_8b_3_out_6, basic_alu_8b_4_out_6);
  Basic_ALU_8b basic_alu_8b_3 (
    .out_4(basic_alu_8b_3_out_4[0]), .Control({Control[5:1], basic_alu_8b_4_out_4[0]}), .A(A[15:8]),
    .B(B[15:8]), .Output(basic_alu_8b_4_output[15:8]), .out_6(basic_alu_8b_3_out_6));
  Basic_ALU_8b basic_alu_8b_4 (
    .out_4(basic_alu_8b_4_out_4[0]), .Control(Control), .A(A[7:0]), .B(B[7:0]),
    .Output(basic_alu_8b_4_output[7:0]), .out_6(basic_alu_8b_4_out_6));
  or or_1 (or_1_out, Control[0], Control[1], Control[2], Control[3], Control[4], Control[5]);

  // Other names for the same wires on the sheet: Flag[1:0] = Flag_NZ
endmodule
