// Logisim project CPU.circ as structural Verilog: 22 circuits, main circuit Program Counter
// PC
module Program_Counter (
  input  [15:0] Input_Bus,
  input  [3:0] OE_L_Ct_Clk,
  output [15:0] Output_Bus
);

  wire d_ff_1_q, HI_carry, LOW_carry;
  wire [7:0] HI_q, LOW_q;

  D_Flip_Flop d_ff_1 (.clk(OE_L_Ct_Clk[3]), .D(OE_L_Ct_Clk[1]), .Q(d_ff_1_q));  // open: Qn, preset, en, reset
  Counter LOW (
    .load(OE_L_Ct_Clk[1]), .D(Input_Bus[7:0]), .count(OE_L_Ct_Clk[2]), .Q(LOW_q), .carry(LOW_carry),
    .clk(OE_L_Ct_Clk[3]), .clr(HI_carry));
  Counter HI (
    .load(d_ff_1_q), .D(Input_Bus[15:8]), .count(LOW_carry), .Q(HI_q), .carry(HI_carry),
    .clk(OE_L_Ct_Clk[3]), .clr(HI_carry));
  assign Output_Bus = OE_L_Ct_Clk[0] ? {HI_q, LOW_q} : 16'bz;  // Controlled_Buffer controlled_buffer_1
endmodule

// CU
module Control_Unit (
  input  Clock,
  input  [7:0] Input,
  input  [7:0] Flag_Input,
  output [31:0] out_4
);

  wire nor_1_out, not_1_out, not_2_out, not_3_out, ring_counter_1_out_5, ring_counter_1_out_21;
  wire [0:0] rom_2_data;
  wire [7:0] counter_1_q, rom_1_data;

  assign out_4[0] = not_2_out ? Clock : 1'bz;  // Controlled_Buffer controlled_buffer_1
  Counter counter_1 (
    .load(not_3_out), .D(rom_1_data), .count(ring_counter_1_out_5), .Q(counter_1_q), .clk(out_4[0]),
    .clr(not_1_out));  // open: carry
  ROM rom_1 (.addr(Input), .data(rom_1_data));  // open: sel
  not not_1 (not_1_out, ring_counter_1_out_21);
  not not_2 (not_2_out, rom_2_data[0]);
  not not_3 (not_3_out, ring_counter_1_out_5);
  ROM rom_2 (.addr(counter_1_q), .data({rom_2_data[0], out_4[31:25]}));  // open: sel
  Ring_Counter ring_counter_1 (
    .in_1(out_4[0]), .Clear(nor_1_out), .out_5(ring_counter_1_out_5), .out_21(ring_counter_1_out_21));  // open: out_3, out_4, out_6, out_7, out_8, out_9, out_10, out_11, out_12, out_13, out_14, out_15, out_16, out_17, out_18, out_19, out_20
  ROM rom_3 (.addr(counter_1_q), .data(out_4[24:17]));  // open: sel
  ROM rom_4 (.addr(counter_1_q), .data(out_4[16:9]));  // open: sel
  ROM rom_5 (.addr(counter_1_q), .data(out_4[8:1]));  // open: sel
  nor nor_1 (nor_1_out, rom_2_data[0], out_4[17], out_4[18], out_4[19], out_4[20], out_4[21], out_4[22], out_4[23], out_4[24], out_4[25], out_4[26], out_4[27], out_4[28], out_4[29], out_4[30], out_4[31], out_4[1], out_4[2], out_4[3], out_4[4], out_4[5], out_4[6], out_4[7], out_4[8], out_4[9], out_4[10], out_4[11], out_4[12], out_4[13], out_4[14], out_4[15], out_4[16]);

  // Notes on the sheet:
  //   contents of rom_1 (hex, n*v repeats v):
  //   0 4 6 8 a c e 10 12 14 16 18 1a 1c 21 23 25 27 29 2b 2d 31 35 39 3b 3d 41
  //   contents of rom_2 (hex, n*v repeats v):
  //   4*0 4 0 4 0 6 0 6 0 7 0 7 0 4 0 4 0 6 0 6 0 7 0 7 0 0 0 5 2 25*0 20 0 40
  //   contents of rom_3 (hex, n*v repeats v):
  //   4*0 10 0 50 0 10 0 70 0 50 0 70 0 10 0 50 0 10 0 70 0 50 0 70 0 0 30 30 10 0 1b 0 52 0 1b 0 72 0 5e
  //   0 7b 0 0 0 10 0 0 0 50 0 0 0 70 0 2 0 2 5*0 10
  //   contents of rom_4 (hex, n*v repeats v):
  //   0 7 0 0 b0 0 b0 0 b0 0 b0 0 b0 0 b0 0 a4 0 a4 0 a4 0 a4 7*0 1 a4 15*0 1 0 0 0 1 0 0 0 1
  //   contents of rom_5 (hex, n*v repeats v):
  //   29 0 4 25*0 d 20 15*0 d 20 0 0 d 20 0 0 d 20 6*0 d 22 d 0 30
endmodule

// MAR
module Memory_Address_Register (
  input  [15:0] Input,
  input  [1:0] IE_Clk,
  output [15:0] Output
);

  Register #(.width(16)) register_1 (.D(Input), .en(IE_Clk[0]), .Q(Output), .clk(IE_Clk[1]), .clr(1'b0));
endmodule

// MEM
module Memory (
  input  [15:0] Address,
  input  [7:0] in_2,
  input  [1:0] L_Clk,
  output [7:0] out_4
);

  wire not_1_out;
  wire [7:0] controlled_buffer_1_out, ram_1_data;

  RAM #(.addrWidth(16), .bus("separate")) ram_1 (
    .addr(Address), .din(controlled_buffer_1_out), .data(ram_1_data), .str(L_Clk[0]), .clk(L_Clk[1]),
    .ld(not_1_out));  // open: sel, clr
  assign controlled_buffer_1_out = L_Clk[0] ? in_2 : 8'bz;  // Controlled_Buffer controlled_buffer_1
  not not_1 (not_1_out, L_Clk[0]);
  assign out_4 = not_1_out ? ram_1_data : 8'bz;  // Controlled_Buffer controlled_buffer_2
endmodule

// MDR
module Memory_Data_Register (
  input  [7:0] In,
  input  [7:0] In_Bus,
  input  [4:0] I_Ibus_O_Obus_Clk,
  output [7:0] Out,
  output [7:0] Out_Bus
);

  wire [7:0] controlled_buffer_1_out, register_1_q;

  assign controlled_buffer_1_out = I_Ibus_O_Obus_Clk[0] ? In : 8'bz;  // Controlled_Buffer controlled_buffer_1
  assign controlled_buffer_1_out = I_Ibus_O_Obus_Clk[1] ? In_Bus : 8'bz;  // Controlled_Buffer controlled_buffer_2
  assign Out = I_Ibus_O_Obus_Clk[2] ? register_1_q : 8'bz;  // Controlled_Buffer controlled_buffer_3
  Register register_1 (
    .D(controlled_buffer_1_out), .en(1'b1), .Q(register_1_q), .clk(I_Ibus_O_Obus_Clk[4]));  // open: clr
  assign Out_Bus = I_Ibus_O_Obus_Clk[3] ? register_1_q : 8'bz;  // Controlled_Buffer controlled_buffer_4
endmodule

// IR
module Instruction_Register (
  input  [7:0] Input,
  input  [1:0] E_Clk,
  output [7:0] Output
);

  Register register_1 (.D(Input), .en(E_Clk[0]), .Q(Output), .clk(E_Clk[1]));  // open: clr
endmodule

// A
module Accumulator_Register (
  input  [7:0] Input_Bus,
  input  [2:0] Obus_Ibus_Clk,
  output [7:0] Output_Bus,
  output [7:0] ALU
);

  assign Output_Bus = Obus_Ibus_Clk[0] ? ALU : 8'bz;  // Controlled_Buffer controlled_buffer_1
  Register register_1 (.D(Input_Bus), .en(Obus_Ibus_Clk[1]), .Q(ALU), .clk(Obus_Ibus_Clk[2]));  // open: clr
endmodule

// TMP
module Temp_Register (
  input  [7:0] Input_Bus,
  input  [2:0] Obus_Ibus_Clk,
  output [7:0] Output_Bus,
  output [7:0] ALU
);

  assign Output_Bus = Obus_Ibus_Clk[0] ? ALU : 8'bz;  // Controlled_Buffer controlled_buffer_1
  Register register_1 (.D(Input_Bus), .en(Obus_Ibus_Clk[1]), .Q(ALU), .clk(Obus_Ibus_Clk[2]));  // open: clr
endmodule

// B
module B_Register (
  input  [7:0] Input_Bus,
  input  [2:0] Obus_Ibus_ALU_Clk,
  output [7:0] ALU,
  output [7:0] Output_Bus
);

  assign Output_Bus = Obus_Ibus_ALU_Clk[0] ? ALU : 8'bz;  // Controlled_Buffer controlled_buffer_1
  Register register_1 (.D(Input_Bus), .en(Obus_Ibus_ALU_Clk[1]), .Q(ALU), .clk(Obus_Ibus_ALU_Clk[2]));  // open: clr
endmodule

// C
module C_Register (
  input  [7:0] Input_Bus,
  input  [2:0] Obus_Ibus_Clk,
  output [7:0] ALU,
  output [7:0] Output_Bus
);

  assign Output_Bus = Obus_Ibus_Clk[0] ? ALU : 8'bz;  // Controlled_Buffer controlled_buffer_1
  Register register_1 (.D(Input_Bus), .en(Obus_Ibus_Clk[1]), .Q(ALU), .clk(Obus_Ibus_Clk[2]));  // open: clr
endmodule

// OP3
module Output_Port_3 (
  input  [7:0] Input,
  input  [1:0] E_Clk,
  output [7:0] Output
);

  Register register_1 (.D(Input), .en(E_Clk[0]), .Q(Output), .clk(E_Clk[1]));  // open: clr
endmodule

// OP4
module Output_Port_4 (
  input  [7:0] Input,
  input  [1:0] E_Clk,
  output [7:0] Output
);

  wire [7:7] register_1_q;

  Register register_1 (.D(Input), .en(E_Clk[0]), .Q({register_1_q[7], Output[6:0]}), .clk(E_Clk[1]));  // open: clr
  D_Flip_Flop d_ff_1 (.clk(E_Clk[1]), .D(E_Clk[0]), .Q(Output[7]));  // open: Qn, preset, en, reset
endmodule

module ALU (
  input  [7:0] A_Input,
  input  [7:0] Op_Lf_Ci_Eo_LSh_Clk,
  input  [7:0] B_Input,
  output [7:0] Output_Bus,
  output [7:0] C_Z
);

  wire alu_cell_1_carry_out, alu_cell_2_carry_out, alu_cell_3_carry_out, alu_cell_4_carry_out,
       alu_cell_5_carry_out, alu_cell_6_carry_out, alu_cell_7_carry_out, alu_cell_8_carry_out, and_1_out,
       nand_1_out, nor_1_out;
  wire [7:0] alu_cell_1_output, controlled_buffer_1_out, rotate_logic_1_f;

  Rotate_Logic rotate_logic_1 (
    .Rotate_R_L_prime(nand_1_out), .Clock(Op_Lf_Ci_Eo_LSh_Clk[7]), .LOAD(Op_Lf_Ci_Eo_LSh_Clk[6]),
    .F(rotate_logic_1_f), .Input(A_Input));
  nand nand_1 (nand_1_out, Op_Lf_Ci_Eo_LSh_Clk[2], Op_Lf_Ci_Eo_LSh_Clk[1], ~Op_Lf_Ci_Eo_LSh_Clk[0]);  // NAND_Gate
  and and_1 (and_1_out, Op_Lf_Ci_Eo_LSh_Clk[2], Op_Lf_Ci_Eo_LSh_Clk[1]);
  assign controlled_buffer_1_out = and_1_out ? rotate_logic_1_f : 8'bz;  // Controlled_Buffer controlled_buffer_1
  ALU_Cell alu_cell_1 (
    .INPUT_A(A_Input[0]), .INPUT_B(B_Input[0]), .OUTPUT(alu_cell_1_output[0]),
    .Rotate_Mux_Input(controlled_buffer_1_out[0]), .OPERATION(Op_Lf_Ci_Eo_LSh_Clk[2:0]),
    .Carry_Out(alu_cell_1_carry_out), .in_3(Op_Lf_Ci_Eo_LSh_Clk[4]));
  ALU_Cell alu_cell_2 (
    .INPUT_A(A_Input[1]), .INPUT_B(B_Input[1]), .OUTPUT(alu_cell_1_output[1]),
    .Rotate_Mux_Input(controlled_buffer_1_out[1]), .OPERATION(Op_Lf_Ci_Eo_LSh_Clk[2:0]),
    .Carry_Out(alu_cell_2_carry_out), .in_3(alu_cell_1_carry_out));
  ALU_Cell alu_cell_3 (
    .INPUT_A(A_Input[2]), .INPUT_B(B_Input[2]), .OUTPUT(alu_cell_1_output[2]),
    .Rotate_Mux_Input(controlled_buffer_1_out[2]), .OPERATION(Op_Lf_Ci_Eo_LSh_Clk[2:0]),
    .Carry_Out(alu_cell_3_carry_out), .in_3(alu_cell_2_carry_out));
  ALU_Cell alu_cell_4 (
    .INPUT_A(A_Input[3]), .INPUT_B(B_Input[3]), .OUTPUT(alu_cell_1_output[3]),
    .Rotate_Mux_Input(controlled_buffer_1_out[3]), .OPERATION(Op_Lf_Ci_Eo_LSh_Clk[2:0]),
    .Carry_Out(alu_cell_4_carry_out), .in_3(alu_cell_3_carry_out));
  ALU_Cell alu_cell_5 (
    .INPUT_A(A_Input[4]), .INPUT_B(B_Input[4]), .OUTPUT(alu_cell_1_output[4]),
    .Rotate_Mux_Input(controlled_buffer_1_out[4]), .OPERATION(Op_Lf_Ci_Eo_LSh_Clk[2:0]),
    .Carry_Out(alu_cell_5_carry_out), .in_3(alu_cell_4_carry_out));
  ALU_Cell alu_cell_6 (
    .INPUT_A(A_Input[5]), .INPUT_B(B_Input[5]), .OUTPUT(alu_cell_1_output[5]),
    .Rotate_Mux_Input(controlled_buffer_1_out[5]), .OPERATION(Op_Lf_Ci_Eo_LSh_Clk[2:0]),
    .Carry_Out(alu_cell_6_carry_out), .in_3(alu_cell_5_carry_out));
  ALU_Cell alu_cell_7 (
    .INPUT_A(A_Input[6]), .INPUT_B(B_Input[6]), .OUTPUT(alu_cell_1_output[6]),
    .Rotate_Mux_Input(controlled_buffer_1_out[6]), .OPERATION(Op_Lf_Ci_Eo_LSh_Clk[2:0]),
    .Carry_Out(alu_cell_7_carry_out), .in_3(alu_cell_6_carry_out));
  ALU_Cell alu_cell_8 (
    .INPUT_A(A_Input[7]), .INPUT_B(B_Input[7]), .OUTPUT(alu_cell_1_output[7]),
    .Rotate_Mux_Input(controlled_buffer_1_out[7]), .OPERATION(Op_Lf_Ci_Eo_LSh_Clk[2:0]),
    .Carry_Out(alu_cell_8_carry_out), .in_3(alu_cell_7_carry_out));
  assign Output_Bus = Op_Lf_Ci_Eo_LSh_Clk[5] ? alu_cell_1_output : 8'bz;  // Controlled_Buffer controlled_buffer_2
  and and_2 (C_Z[7], alu_cell_8_carry_out, Op_Lf_Ci_Eo_LSh_Clk[3]);
  nor nor_1 (nor_1_out, alu_cell_1_output[7], alu_cell_1_output[6], alu_cell_1_output[5], alu_cell_1_output[4], alu_cell_1_output[3], alu_cell_1_output[2], alu_cell_1_output[1], alu_cell_1_output[0]);
  and and_3 (C_Z[3], Op_Lf_Ci_Eo_LSh_Clk[3], nor_1_out);

  assign {C_Z[6:4], C_Z[2:0]} = {{3{C_Z[7]}}, {3{C_Z[3]}}};

  // Notes on the sheet:
  //   0- CMA - Complementary of A
  //   1- AND x - A AND x
  //   2- OR x - A OR x
  //   3- XOR x - A XOR x
  //   4- ADD x -  A+x
  //   5- SUB x -  A-x
  //   6- RAL - Rotate A Left
  //   7- RAR - Rotate A Right
endmodule

// IP1
module Input_Port_1 (
  input  [7:0] Input,
  input  Clock,
  output [7:0] Output
);

  DotMatrix #(.matrixcols(7), .matrixrows(1)) dotmatrix_1 (
    .col0(Input[6]), .col1(Input[5]), .col2(Input[4]), .col3(Input[3]), .col4(Input[2]), .col5(Input[1]),
    .col6(Input[0]));
  Register register_1 (.D(Input), .en(Input[7]), .Q(Output), .clk(Clock));  // open: clr
endmodule

// IP
module Input (
  input  [7:0] in_1,
  input  [7:0] in_2,
  input  Clock,
  input  [1:0] in_4,
  output [7:0] out_5
);

  wire decoder_1_out0, decoder_1_out1;
  wire [7:0] input_port_1_1_output, input_port_1_2_output;

  Input_Port_1 input_port_1_1 (.Input(in_1), .Clock(Clock), .Output(input_port_1_1_output));
  Input_Port_1 input_port_1_2 (.Input(in_2), .Clock(Clock), .Output(input_port_1_2_output));
  assign out_5 = decoder_1_out0 ? input_port_1_1_output : 8'bz;  // Controlled_Buffer controlled_buffer_1
  Decoder #(.disabled(0)) decoder_1 (.out0(decoder_1_out0), .out1(decoder_1_out1), .sel(in_4[1]), .en(in_4[0]));
  assign out_5 = decoder_1_out1 ? input_port_1_2_output : 8'bz;  // Controlled_Buffer controlled_buffer_2
endmodule

// FR
module Flag_Register (
  input  [7:0] Flag_Input,
  input  Clock,
  output [7:0] Flag_Out
);

  Register register_1 (.D(Flag_Input), .en(1'b1), .Q(Flag_Out), .clk(Clock));  // open: clr
endmodule

module ALU_Cell (
  input  INPUT_A,
  input  INPUT_B,
  input  in_3,
  input  [2:0] OPERATION,
  input  Rotate_Mux_Input,
  output OUTPUT,
  output Carry_Out
);

  wire and_1_out, and_2_out, and_3_out, and_4_out, not_1_out, or_1_out, xor_1_out, xor_2_out, xor_3_out,
       xor_4_out;

  xor xor_1 (xor_1_out, INPUT_B, and_4_out);
  not not_1 (not_1_out, INPUT_A);
  and and_1 (and_1_out, INPUT_A, xor_1_out);
  or or_1 (or_1_out, INPUT_A, xor_1_out);
  xor xor_2 (xor_2_out, INPUT_A, xor_1_out);
  xor xor_3 (xor_3_out, INPUT_A, xor_1_out);
  xor xor_4 (xor_4_out, xor_3_out, in_3);
  and and_2 (and_2_out, in_3, xor_3_out);
  and and_3 (and_3_out, INPUT_A, xor_1_out);
  and and_4 (and_4_out, OPERATION[0], ~OPERATION[1], OPERATION[2]);  // AND_Gate
  or or_2 (Carry_Out, and_2_out, and_3_out);
  Multiplexer #(.select(3), .enable("false")) multiplexer_1 (
    .in0(not_1_out), .in1(and_1_out), .in2(or_1_out), .in3(xor_2_out), .in4(xor_4_out), .in5(xor_4_out),
    .in6(Rotate_Mux_Input), .in7(Rotate_Mux_Input), .out(OUTPUT), .sel(OPERATION));

  // Notes on the sheet:
  //   0- CMA - Complementary of A
  //   1- AND x - A AND x
  //   2- OR x - A OR x
  //   3- XOR x - A XOR x
  //   4- ADD x -  A+x
  //   5- SUB x -  A-x
  //   6- RAL - Rotate A Left
  //   7- RAR - Rotate A Right
  //   4-NOP
  //   5-HLT
  //   6- IN - INPUT
  //   7- OUT - OUTPUT
  //   12- MOV x,k - x=k
  //   13- CALL a
  //   14- RET
  //   15- STA a - STORE A to address
  //   16- INC x - Increment
  //   17- DIC x - Dicrement
  //   18- JMP a
  //   19- JM a - Jump if minus
  //   20- JZ a 
  //   21- JNZ a 
  //   Instead of immediate istruction we use OPCODE I,Var
endmodule

module Rotate_Logic (
  input  Rotate_R_L_prime,
  input  Clock,
  input  LOAD,
  input  [7:0] Input,
  output [7:0] F
);

  wire and_1_out, and_2_out, and_3_out, and_4_out, and_5_out, and_6_out, and_7_out, and_8_out, j_k_ff_1_qn,
       j_k_ff_2_qn, j_k_ff_3_qn, j_k_ff_4_qn, j_k_ff_5_qn, j_k_ff_6_qn, j_k_ff_7_qn, j_k_ff_8_qn, nand_1_out,
       nand_2_out, nand_3_out, nand_4_out, nand_5_out, nand_6_out, nand_7_out, nand_8_out, nand_9_out,
       nand_10_out, nand_11_out, nand_12_out, nand_13_out, nand_14_out, nand_15_out, nand_16_out, not_1_out,
       not_2_out, not_3_out, not_4_out, not_5_out, not_6_out, not_7_out, not_8_out, not_9_out, not_10_out,
       not_11_out, not_12_out, not_13_out, not_14_out, not_15_out, not_16_out;
  wire [7:0] controlled_buffer_1_out;

  nand nand_1 (nand_1_out, ~Rotate_R_L_prime, j_k_ff_2_qn);  // NAND_Gate
  nand nand_2 (nand_2_out, j_k_ff_8_qn, Rotate_R_L_prime);
  and and_1 (and_1_out, nand_2_out, nand_1_out);
  not not_1 (not_1_out, and_1_out);
  nand nand_3 (nand_3_out, ~Rotate_R_L_prime, j_k_ff_3_qn);  // NAND_Gate
  nand nand_4 (nand_4_out, j_k_ff_1_qn, Rotate_R_L_prime);
  and and_2 (and_2_out, nand_4_out, nand_3_out);
  J_K_Flip_Flop j_k_ff_1 (
    .J(and_1_out), .clk(Clock), .K(not_1_out), .Q(F[7]), .Qn(j_k_ff_1_qn),
    .preset(controlled_buffer_1_out[7]), .en(1'b1), .reset(not_3_out));
  not not_2 (not_2_out, and_2_out);
  not not_3 (not_3_out, controlled_buffer_1_out[7]);
  nand nand_5 (nand_5_out, j_k_ff_2_qn, Rotate_R_L_prime);
  nand nand_6 (nand_6_out, ~Rotate_R_L_prime, j_k_ff_4_qn);  // NAND_Gate
  and and_3 (and_3_out, nand_5_out, nand_6_out);
  J_K_Flip_Flop j_k_ff_2 (
    .J(and_2_out), .clk(Clock), .K(not_2_out), .Q(F[6]), .Qn(j_k_ff_2_qn),
    .preset(controlled_buffer_1_out[6]), .en(1'b1), .reset(not_5_out));
  not not_4 (not_4_out, and_3_out);
  not not_5 (not_5_out, controlled_buffer_1_out[6]);
  nand nand_7 (nand_7_out, ~Rotate_R_L_prime, j_k_ff_5_qn);  // NAND_Gate
  nand nand_8 (nand_8_out, j_k_ff_3_qn, Rotate_R_L_prime);
  and and_4 (and_4_out, nand_8_out, nand_7_out);
  J_K_Flip_Flop j_k_ff_3 (
    .J(and_3_out), .clk(Clock), .K(not_4_out), .Q(F[5]), .Qn(j_k_ff_3_qn),
    .preset(controlled_buffer_1_out[5]), .en(1'b1), .reset(not_7_out));
  not not_6 (not_6_out, and_4_out);
  not not_7 (not_7_out, controlled_buffer_1_out[5]);
  assign controlled_buffer_1_out = LOAD ? Input : 8'bz;  // Controlled_Buffer controlled_buffer_1
  nand nand_9 (nand_9_out, ~Rotate_R_L_prime, j_k_ff_6_qn);  // NAND_Gate
  nand nand_10 (nand_10_out, j_k_ff_4_qn, Rotate_R_L_prime);
  and and_5 (and_5_out, nand_10_out, nand_9_out);
  J_K_Flip_Flop j_k_ff_4 (
    .J(and_4_out), .clk(Clock), .K(not_6_out), .Q(F[4]), .Qn(j_k_ff_4_qn),
    .preset(controlled_buffer_1_out[4]), .en(1'b1), .reset(not_9_out));
  not not_8 (not_8_out, and_5_out);
  not not_9 (not_9_out, controlled_buffer_1_out[4]);
  nand nand_11 (nand_11_out, ~Rotate_R_L_prime, j_k_ff_7_qn);  // NAND_Gate
  nand nand_12 (nand_12_out, j_k_ff_5_qn, Rotate_R_L_prime);
  and and_6 (and_6_out, nand_12_out, nand_11_out);
  J_K_Flip_Flop j_k_ff_5 (
    .J(and_5_out), .clk(Clock), .K(not_8_out), .Q(F[3]), .Qn(j_k_ff_5_qn),
    .preset(controlled_buffer_1_out[3]), .en(1'b1), .reset(not_11_out));
  not not_10 (not_10_out, and_6_out);
  not not_11 (not_11_out, controlled_buffer_1_out[3]);
  nand nand_13 (nand_13_out, j_k_ff_6_qn, Rotate_R_L_prime);
  nand nand_14 (nand_14_out, ~Rotate_R_L_prime, j_k_ff_8_qn);  // NAND_Gate
  and and_7 (and_7_out, nand_13_out, nand_14_out);
  J_K_Flip_Flop j_k_ff_6 (
    .J(and_6_out), .clk(Clock), .K(not_10_out), .Q(F[2]), .Qn(j_k_ff_6_qn),
    .preset(controlled_buffer_1_out[2]), .en(1'b1), .reset(not_13_out));
  not not_12 (not_12_out, and_7_out);
  not not_13 (not_13_out, controlled_buffer_1_out[2]);
  nand nand_15 (nand_15_out, ~Rotate_R_L_prime, j_k_ff_1_qn);  // NAND_Gate
  nand nand_16 (nand_16_out, j_k_ff_7_qn, Rotate_R_L_prime);
  and and_8 (and_8_out, nand_16_out, nand_15_out);
  J_K_Flip_Flop j_k_ff_7 (
    .J(and_7_out), .clk(Clock), .K(not_12_out), .Q(F[1]), .Qn(j_k_ff_7_qn),
    .preset(controlled_buffer_1_out[1]), .en(1'b1), .reset(not_15_out));
  not not_14 (not_14_out, and_8_out);
  not not_15 (not_15_out, controlled_buffer_1_out[1]);
  J_K_Flip_Flop j_k_ff_8 (
    .J(and_8_out), .clk(Clock), .K(not_14_out), .Q(F[0]), .Qn(j_k_ff_8_qn),
    .preset(controlled_buffer_1_out[0]), .en(1'b1), .reset(not_16_out));
  not not_16 (not_16_out, controlled_buffer_1_out[0]);
endmodule

module CPU (
  input  [7:0] Input1,
  input  [7:0] Input2,
  input  Clock,
  output [7:0] Output3,
  output [7:0] Output4
);

  wire Clock_t, IR, MAR, MEM, OP3, OP4;
  wire [1:0] IP;
  wire [2:0] PC;
  wire [3:0] MDR;
  wire [6:0] ALU;
  wire [7:0] alu_1_c_z, Flag, instruction_register_1_output, memory_1_out_4, registers_1_source_a,
       registers_1_source_b, W_8_Bus;
  wire [9:0] Registers;
  wire [15:0] memory_address_register_1_output;
  wire [15:8] W_Bus;

  // Probe on PC
  DotMatrix #(.matrixcols(32), .matrixrows(1)) dotmatrix_1 (
    .col0(OP4), .col1(OP3), .col2(IP[1]), .col3(IP[0]), .col4(Registers[9]), .col5(Registers[8]),
    .col6(Registers[7]), .col7(Registers[6]), .col8(Registers[5]), .col9(Registers[4]), .col10(Registers[3]),
    .col11(Registers[2]), .col12(Registers[1]), .col13(Registers[0]), .col14(ALU[6]), .col15(ALU[5]),
    .col16(ALU[4]), .col17(ALU[3]), .col18(ALU[2]), .col19(ALU[1]), .col20(ALU[0]), .col21(IR),
    .col22(MDR[3]), .col23(MDR[2]), .col24(MDR[1]), .col25(MDR[0]), .col26(MEM), .col27(MAR), .col28(PC[2]),
    .col29(PC[1]), .col30(PC[0]), .col31(Clock_t));
  DotMatrix #(.matrixcols(8), .matrixrows(1)) dotmatrix_2 (
    .col0(instruction_register_1_output[7]), .col1(instruction_register_1_output[6]),
    .col2(instruction_register_1_output[5]), .col3(instruction_register_1_output[4]),
    .col4(instruction_register_1_output[3]), .col5(instruction_register_1_output[2]),
    .col6(instruction_register_1_output[1]), .col7(instruction_register_1_output[0]));
  DotMatrix #(.matrixcols(16), .matrixrows(1)) dotmatrix_3 (
    .col0(W_Bus[15]), .col1(W_Bus[14]), .col2(W_Bus[13]), .col3(W_Bus[12]), .col4(W_Bus[11]),
    .col5(W_Bus[10]), .col6(W_Bus[9]), .col7(W_Bus[8]), .col8(W_8_Bus[7]), .col9(W_8_Bus[6]),
    .col10(W_8_Bus[5]), .col11(W_8_Bus[4]), .col12(W_8_Bus[3]), .col13(W_8_Bus[2]), .col14(W_8_Bus[1]),
    .col15(W_8_Bus[0]));
  Program_Counter program_counter_1 (
    .OE_L_Ct_Clk({Clock_t, PC}), .Input_Bus({W_Bus, W_8_Bus}), .Output_Bus({W_Bus, W_8_Bus}));
  Input input_1 (.in_1(Input1), .Clock(Clock_t), .out_5(W_8_Bus), .in_4(IP), .in_2(Input2));
  // Probe on MAR
  // Probe on MEM
  // Probe on MDR
  // Probe on {W_Bus, W_8_Bus}
  Memory_Address_Register memory_address_register_1 (
    .Input({W_Bus, W_8_Bus}), .Output(memory_address_register_1_output), .IE_Clk({Clock_t, MAR}));
  Memory memory_1 (
    .Address(memory_address_register_1_output), .out_4(memory_1_out_4), .L_Clk({Clock_t, MEM}),
    .in_2(memory_1_out_4));
  Memory_Data_Register memory_data_register_1 (
    .In_Bus(W_8_Bus), .In(memory_1_out_4), .Out(memory_1_out_4), .I_Ibus_O_Obus_Clk({Clock_t, MDR}),
    .Out_Bus(W_8_Bus));
  Instruction_Register instruction_register_1 (
    .Input(W_8_Bus), .Output(instruction_register_1_output), .E_Clk({Clock_t, IR}));
  Control_Unit control_unit_1 (
    .Input(instruction_register_1_output),
    .out_4({OP4, OP3, IP, Registers, ALU, IR, MDR, MEM, MAR, PC, Clock_t}), .Clock(Clock), .Flag_Input(Flag));
  DotMatrix #(.matrixcols(16), .matrixrows(1)) dotmatrix_4 (
    .col0(memory_address_register_1_output[15]), .col1(memory_address_register_1_output[14]),
    .col2(memory_address_register_1_output[13]), .col3(memory_address_register_1_output[12]),
    .col4(memory_address_register_1_output[11]), .col5(memory_address_register_1_output[10]),
    .col6(memory_address_register_1_output[9]), .col7(memory_address_register_1_output[8]),
    .col8(memory_address_register_1_output[7]), .col9(memory_address_register_1_output[6]),
    .col10(memory_address_register_1_output[5]), .col11(memory_address_register_1_output[4]),
    .col12(memory_address_register_1_output[3]), .col13(memory_address_register_1_output[2]),
    .col14(memory_address_register_1_output[1]), .col15(memory_address_register_1_output[0]));
  Pull_Resistor pull_resistor_1 (.node({W_Bus, W_8_Bus}));
  DotMatrix #(.matrixcols(8), .matrixrows(1)) dotmatrix_5 (
    .col0(memory_1_out_4[7]), .col1(memory_1_out_4[6]), .col2(memory_1_out_4[5]), .col3(memory_1_out_4[4]),
    .col4(memory_1_out_4[3]), .col5(memory_1_out_4[2]), .col6(memory_1_out_4[1]), .col7(memory_1_out_4[0]));
  // Probe on PC
  // Probe on MDR
  ALU alu_1 (
    .Output_Bus(W_8_Bus), .A_Input(registers_1_source_a), .B_Input(registers_1_source_b),
    .Op_Lf_Ci_Eo_LSh_Clk({Clock_t, ALU}), .C_Z(alu_1_c_z));
  Registers registers_1 (
    .out_3(W_8_Bus), .in_1(W_8_Bus), .Source_A(registers_1_source_a), .Source_B(registers_1_source_b),
    .in_2({Clock_t, Registers}));
  Output_Port_3 output_port_3_1 (.Input(W_8_Bus), .Output(Output3), .E_Clk({Clock_t, OP3}));
  Output_Port_4 output_port_4_1 (.Input(W_8_Bus), .Output(Output4), .E_Clk({Clock_t, OP4}));
  // Probe on ALU
  // Probe on Flag
  Flag_Register flag_register_1 (.Flag_Input(alu_1_c_z), .Flag_Out(Flag), .Clock(Clock_t));
  Hex_Digit_Display hex_digit_display_1 (.value(Output3[7:4]));  // open: dp
  Hex_Digit_Display hex_digit_display_2 (.value(Output3[3:0]));  // open: dp

  // Other names for the same wires on the sheet: W_Bus[7:0] = W_8_Bus
endmodule

module Ring_Counter (
  input  in_1,
  input  Clear,
  output out_3,
  output out_4,
  output out_5,
  output out_6,
  output out_7,
  output out_8,
  output out_9,
  output out_10,
  output out_11,
  output out_12,
  output out_13,
  output out_14,
  output out_15,
  output out_16,
  output out_17,
  output out_18,
  output out_19,
  output out_20,
  output out_21
);

  wire d_ff_1_q, d_ff_2_q, d_ff_3_q, d_ff_4_q, d_ff_5_q, d_ff_6_q, d_ff_7_q, d_ff_8_q, d_ff_9_q, d_ff_10_q,
       d_ff_11_q, d_ff_12_q, d_ff_13_q, d_ff_14_q, d_ff_15_q, d_ff_16_q, d_ff_17_q, d_ff_18_q, not_1_out;

  D_Flip_Flop d_ff_1 (.clk(in_1), .D(not_1_out), .Q(d_ff_1_q), .Qn(out_3), .en(1'b1), .reset(Clear));  // open: preset
  D_Flip_Flop d_ff_2 (.clk(in_1), .D(d_ff_1_q), .Q(d_ff_2_q), .Qn(out_4), .en(1'b1), .reset(Clear));  // open: preset
  D_Flip_Flop d_ff_3 (.clk(in_1), .D(d_ff_2_q), .Q(d_ff_3_q), .Qn(out_5), .en(1'b1), .reset(Clear));  // open: preset
  D_Flip_Flop d_ff_4 (.clk(in_1), .D(d_ff_3_q), .Q(d_ff_4_q), .Qn(out_6), .en(1'b1), .reset(Clear));  // open: preset
  D_Flip_Flop d_ff_5 (.clk(in_1), .D(d_ff_4_q), .Q(d_ff_5_q), .Qn(out_7), .en(1'b1), .reset(Clear));  // open: preset
  D_Flip_Flop d_ff_6 (.clk(in_1), .D(d_ff_5_q), .Q(d_ff_6_q), .Qn(out_8), .en(1'b1), .reset(Clear));  // open: preset
  D_Flip_Flop d_ff_7 (.clk(in_1), .D(d_ff_6_q), .Q(d_ff_7_q), .Qn(out_9), .en(1'b1), .reset(Clear));  // open: preset
  D_Flip_Flop d_ff_8 (.clk(in_1), .D(d_ff_7_q), .Q(d_ff_8_q), .Qn(out_10), .en(1'b1), .reset(Clear));  // open: preset
  D_Flip_Flop d_ff_9 (.clk(in_1), .D(d_ff_8_q), .Q(d_ff_9_q), .Qn(out_11), .en(1'b1), .reset(Clear));  // open: preset
  D_Flip_Flop d_ff_10 (.clk(in_1), .D(d_ff_9_q), .Q(d_ff_10_q), .Qn(out_12), .en(1'b1), .reset(Clear));  // open: preset
  D_Flip_Flop d_ff_11 (
    .clk(in_1), .D(d_ff_10_q), .Q(d_ff_11_q), .Qn(out_13), .en(1'b1), .reset(Clear));  // open: preset
  D_Flip_Flop d_ff_12 (
    .clk(in_1), .D(d_ff_11_q), .Q(d_ff_12_q), .Qn(out_14), .en(1'b1), .reset(Clear));  // open: preset
  D_Flip_Flop d_ff_13 (
    .clk(in_1), .D(d_ff_12_q), .Q(d_ff_13_q), .Qn(out_15), .en(1'b1), .reset(Clear));  // open: preset
  D_Flip_Flop d_ff_14 (
    .clk(in_1), .D(d_ff_13_q), .Q(d_ff_14_q), .Qn(out_16), .en(1'b1), .reset(Clear));  // open: preset
  D_Flip_Flop d_ff_15 (
    .clk(in_1), .D(d_ff_14_q), .Q(d_ff_15_q), .Qn(out_17), .en(1'b1), .reset(Clear));  // open: preset
  D_Flip_Flop d_ff_16 (
    .clk(in_1), .D(d_ff_15_q), .Q(d_ff_16_q), .Qn(out_18), .en(1'b1), .reset(Clear));  // open: preset
  D_Flip_Flop d_ff_17 (
    .clk(in_1), .D(d_ff_16_q), .Q(d_ff_17_q), .Qn(out_19), .en(1'b1), .reset(Clear));  // open: preset
  D_Flip_Flop d_ff_18 (
    .clk(in_1), .D(d_ff_17_q), .Q(d_ff_18_q), .Qn(out_20), .en(1'b1), .reset(Clear));  // open: preset
  not not_1 (not_1_out, out_21);
  or or_1 (out_21, d_ff_4_q, d_ff_3_q, d_ff_2_q, d_ff_1_q, d_ff_5_q, d_ff_6_q, d_ff_7_q, d_ff_8_q, d_ff_9_q, d_ff_10_q, d_ff_11_q, d_ff_12_q, d_ff_13_q, d_ff_14_q, d_ff_15_q, d_ff_16_q, d_ff_17_q, d_ff_18_q);

  // Notes on the sheet:
  //   D' Ring Counter
endmodule

module Computer (
  input  in_1,
  input  in_2
);

  wire clock_1_out;
  wire [6:0] keyboard_1_data;
  wire [7:0] cpu_1_output3, cpu_1_output4;
  wire [7:7] keyboard_1_avail;

  Keyboard keyboard_1 (.clk(clock_1_out), .re(in_1), .clr(in_2), .avail(keyboard_1_avail[7]), .data(keyboard_1_data));
  CPU cpu_1 (
    .Output3(cpu_1_output3), .Output4(cpu_1_output4), .Input1({keyboard_1_avail[7], keyboard_1_data}),
    .Clock(clock_1_out));  // open: Input2
  Clock clock_1 (.out(clock_1_out));
  Hex_Digit_Display hex_digit_display_1 (.value(cpu_1_output3[3:0]));  // open: dp
  Hex_Digit_Display hex_digit_display_2 (.value(cpu_1_output3[7:4]));  // open: dp
  TTY tty_1 (.data(cpu_1_output4[6:0]), .clk(clock_1_out), .we(cpu_1_output4[7]));  // open: clr
endmodule

// Reg
module Registers (
  input  [7:0] in_1,
  input  [10:0] in_2,
  output [7:0] out_3,
  output [7:0] Source_A,
  output [7:0] Source_B
);

  wire [1:0] decoder_2_out0, decoder_2_out1, decoder_2_out2, decoder_2_out3;
  wire [7:0] accumulator_register_1_alu, b_register_1_alu, c_register_1_alu, temp_register_1_alu;

  Accumulator_Register accumulator_register_1 (
    .Output_Bus(out_3), .Input_Bus(in_1), .ALU(accumulator_register_1_alu),
    .Obus_Ibus_Clk({in_2[10], decoder_2_out0}));
  Temp_Register temp_register_1 (
    .Output_Bus(out_3), .Input_Bus(in_1), .ALU(temp_register_1_alu),
    .Obus_Ibus_Clk({in_2[10], decoder_2_out1}));
  B_Register b_register_1 (
    .Output_Bus(out_3), .Input_Bus(in_1), .Obus_Ibus_ALU_Clk({in_2[10], decoder_2_out2}),
    .ALU(b_register_1_alu));
  C_Register c_register_1 (
    .Output_Bus(out_3), .Input_Bus(in_1), .Obus_Ibus_Clk({in_2[10], decoder_2_out3}), .ALU(c_register_1_alu));
  // Probe on in_2[9:8]
  Decoder #(.select(2), .disabled(0)) decoder_1 (
    .out0(decoder_2_out0[1]), .out1(decoder_2_out1[1]), .out2(decoder_2_out2[1]), .out3(decoder_2_out3[1]),
    .sel(in_2[5:4]), .en(in_2[3]));
  // Probe on in_2[5:4]
  Multiplexer #(.select(2), .width(8), .enable("false")) multiplexer_1 (
    .in0(accumulator_register_1_alu), .in1(temp_register_1_alu), .in2(b_register_1_alu),
    .in3(c_register_1_alu), .out(Source_A), .sel(in_2[7:6]));
  // Probe on in_2[7:6]
  Multiplexer #(.select(2), .width(8), .enable("false")) multiplexer_2 (
    .in0(accumulator_register_1_alu), .in1(temp_register_1_alu), .in2(b_register_1_alu),
    .in3(c_register_1_alu), .out(Source_B), .sel(in_2[9:8]));
  Decoder #(.select(2), .disabled(0)) decoder_2 (
    .out0(decoder_2_out0[0]), .out1(decoder_2_out1[0]), .out2(decoder_2_out2[0]), .out3(decoder_2_out3[0]),
    .sel(in_2[2:1]), .en(in_2[0]));
  // Probe on in_2[2:1]
  LED led_1 (.in(accumulator_register_1_alu[7]));
  LED led_2 (.in(accumulator_register_1_alu[6]));
  LED led_3 (.in(accumulator_register_1_alu[4]));
  LED led_4 (.in(accumulator_register_1_alu[3]));
  LED led_5 (.in(accumulator_register_1_alu[5]));
  LED led_6 (.in(accumulator_register_1_alu[1]));
  LED led_7 (.in(accumulator_register_1_alu[2]));
  LED led_8 (.in(accumulator_register_1_alu[0]));

  // Other names for the same wires on the sheet: Clock = in_2[10]

  // Notes on the sheet:
  //   REG IN
  //   BUS OUT
endmodule
