// Logisim project tanenbaumMic1CPU.circ as structural Verilog: 6 circuits, main circuit main
module main (
);

  wire clock_1_out, clock_2_out, clock_3_out, clock_4_out, clock_5_out, decoder_1_out0, decoder_1_out1,
       decoder_1_out2, decoder_1_out3, M0, M1, M2, M3, or_5_out;
  wire [1:0] W_R;
  wire [7:0] ram_1_data, ram_2_data, ram_3_data, ram_4_data;
  wire [31:0] cpu_1_mem_addr, cpu_1_mem_out;

  Decoder #(.select(2), .enable("false")) decoder_1 (
    .out0(decoder_1_out0), .out1(decoder_1_out1), .out2(decoder_1_out2), .out3(decoder_1_out3),
    .sel(cpu_1_mem_addr[1:0]));
  CPU cpu_1 (
    .MEM_ADDR(cpu_1_mem_addr), .MEM_IN({ram_4_data, ram_3_data, ram_2_data, ram_1_data}),
    .MEM_OUT(cpu_1_mem_out), .Clock(clock_1_out), .out_5(W_R));
  Clock clock_1 (.out(clock_1_out));
  Clock clock_2 (.out(clock_2_out));
  Clock clock_3 (.out(clock_3_out));
  Clock clock_4 (.out(clock_4_out));
  Clock clock_5 (.out(clock_5_out));
  or or_1 (M0, or_5_out, decoder_1_out0);
  or or_2 (M1, or_5_out, decoder_1_out1);
  RAM #(.addrWidth(24), .bus("separate")) ram_1 (
    .addr(cpu_1_mem_addr[25:2]), .din(cpu_1_mem_out[7:0]), .data(ram_1_data), .str(W_R[1]), .sel(M0),
    .clk(clock_2_out));  // open: ld, clr
  RAM #(.addrWidth(24), .bus("separate")) ram_2 (
    .addr(cpu_1_mem_addr[25:2]), .din(cpu_1_mem_out[15:8]), .data(ram_2_data), .str(W_R[1]), .sel(M1),
    .clk(clock_3_out));  // open: ld, clr
  RAM #(.addrWidth(24), .bus("separate")) ram_3 (
    .addr(cpu_1_mem_addr[25:2]), .din(cpu_1_mem_out[23:16]), .data(ram_3_data), .str(W_R[1]), .sel(M2),
    .clk(clock_4_out));  // open: ld, clr
  RAM #(.addrWidth(24), .bus("separate")) ram_4 (
    .addr(cpu_1_mem_addr[25:2]), .din(cpu_1_mem_out[31:24]), .data(ram_4_data), .str(W_R[1]), .sel(M3),
    .clk(clock_5_out));  // open: ld, clr
  or or_3 (M2, or_5_out, decoder_1_out2);
  or or_4 (M3, or_5_out, decoder_1_out3);
  or or_5 (or_5_out, W_R[0], W_R[1]);
  // Probe on {ram_4_data, ram_3_data, ram_2_data, ram_1_data}
endmodule

module CPU (
  input  [31:0] MEM_IN,
  input  Clock,
  output [31:0] MEM_ADDR,
  output [31:0] MEM_OUT,
  output [1:0] out_5
);

  wire C0, C1, C2, C3, C4;
  wire [0:0] M;
  wire [1:0] ALU_Sh, Flag;
  wire [3:0] B;
  wire [5:0] ALU_Ctrl;
  wire [7:0] MDRIN, multiplexer_1_out, registers_1_mbr;
  wire [8:0] C;
  wire [31:0] basic_alu_32b_1_output, latch_1_out_2, latch_2_out_2, MEM, registers_1_a, registers_1_b,
       registers_1_mem_2, shifter_1_out_4;

  Timing timing_1 (.Clk(Clock), .out_2(C0), .out_3(C1), .out_4(C2), .out_5(C3), .out_6(C4));
  Multiplexer #(.select(2), .width(8), .enable("false")) multiplexer_1 (
    .in0(MEM[7:0]), .in1(MEM[15:8]), .in2(MEM[23:16]), .in3(MEM[31:24]), .out(multiplexer_1_out),
    .sel(MEM_ADDR[1:0]));
  Registers registers_1 (
    .MControl({out_5, M[0]}), .RegIn(C), .RegOut(B), .Clk(C3), .C_Bus(shifter_1_out_4), .A(registers_1_a),
    .B(registers_1_b), .MEM(MEM), .MEM_2(registers_1_mem_2), .MAddr(MEM_ADDR), .MBR(registers_1_mbr),
    .MBR_IN(MDRIN));
  Latch latch_1 (.in_1(registers_1_a), .out_2(latch_1_out_2));
  assign MEM = MEM_IN;  // Buffer buffer_1, 32 bits wide
  assign MEM_OUT = registers_1_mem_2;  // Buffer buffer_2, 32 bits wide
  Latch latch_2 (.in_1(registers_1_b), .out_2(latch_2_out_2));
  Basic_ALU_32b basic_alu_32b_1 (
    .Control(ALU_Ctrl), .Flag_NZ(Flag), .A(latch_1_out_2), .B(latch_2_out_2), .Output(basic_alu_32b_1_output));  // open: out_4
  Shifter shifter_1 (.in_1(basic_alu_32b_1_output), .out_4(shifter_1_out_4), .Clk(C2), .in_2(ALU_Sh));
  assign MDRIN = M[0] ? multiplexer_1_out : 8'bz;  // Controlled_Buffer controlled_buffer_1
  Control control_1 (
    .MBR(registers_1_mbr), .Flag_NZ(Flag), .Clk(C0), .ALU_Sh(ALU_Sh), .ALU_Control(ALU_Ctrl), .C(C),
    .M({out_5, M[0]}), .B(B));

  // Other names for the same wires on the sheet: M[2:1] = out_5; MAddr[31:0] = MEM_ADDR
endmodule

module Registers (
  input  [31:0] MEM,
  input  [7:0] MBR_IN,
  input  [2:0] MControl,
  input  [8:0] RegIn,
  input  [3:0] RegOut,
  input  [31:0] C_Bus,
  input  Clk,
  output [31:0] MEM_2,
  output [31:0] MAddr,
  output [7:0] MBR,
  output [31:0] A,
  output [31:0] B
);

  wire buffer_1_out, nor_1_out, not_1_out, or_1_out;
  wire [1:0] pull_resistor_2_node;
  wire [31:0] bit_extender_1_out, bit_extender_2_out, controlled_buffer_1_out, CPP_q, LV_q, MAR_q, MDR_q,
       MEMIN, OPC_q, PC_q, SP_q, TOS_q;

  assign controlled_buffer_1_out = MControl[1] ? MEMIN : 32'bz;  // Controlled_Buffer controlled_buffer_1
  buf buffer_1 (buffer_1_out, RegIn[1]);
  buf buffer_2 (buffer_1_out, MControl[1]);
  Register u_MBR (.D(MBR_IN), .en(MControl[0]), .Q(MBR), .clk(Clk));  // open: clr
  Register #(.width(32)) MAR (.D(C_Bus), .en(RegIn[0]), .Q(MAR_q), .clk(Clk));  // open: clr
  assign controlled_buffer_1_out = not_1_out ? C_Bus : 32'bz;  // Controlled_Buffer controlled_buffer_2
  Register #(.width(32), .trigger("falling")) MDR (
    .D(controlled_buffer_1_out), .en(buffer_1_out), .Q(MDR_q), .clk(Clk));  // open: clr
  Pull_Resistor pull_resistor_1 (.node(buffer_1_out));
  not not_1 (not_1_out, MControl[1]);
  Register #(.width(32)) PC (.D(C_Bus), .en(RegIn[2]), .Q(PC_q), .clk(Clk));  // open: clr
  assign bit_extender_1_out = {{24{MBR[7]}}, MBR};  // Bit_Extender bit_extender_1
  assign bit_extender_2_out = {{24{1'b0}}, MBR};  // Bit_Extender bit_extender_2
  Register #(.width(32)) SP (.D(C_Bus), .en(RegIn[3]), .Q(SP_q), .clk(Clk));  // open: clr
  Register #(.width(32)) LV (.D(C_Bus), .en(RegIn[4]), .Q(LV_q), .clk(Clk));  // open: clr
  Register #(.width(32)) CPP (.D(C_Bus), .en(RegIn[5]), .Q(CPP_q), .clk(Clk));  // open: clr
  Register #(.width(32)) TOS (.D(C_Bus), .en(RegIn[6]), .Q(TOS_q), .clk(Clk));  // open: clr
  Register #(.width(32)) OPC (.D(C_Bus), .en(RegIn[7]), .Q(OPC_q), .clk(Clk));  // open: clr
  Register #(.width(32)) H (.D(C_Bus), .en(RegIn[8]), .Q(A), .clk(Clk));  // open: clr
  Pull_Resistor pull_resistor_2 (.node(pull_resistor_2_node));
  assign MAddr = or_1_out ? {MAR_q[29:0], pull_resistor_2_node} : 32'bz;  // Controlled_Buffer controlled_buffer_3
  or or_1 (or_1_out, MControl[1], MControl[2]);
  assign MEM_2 = MControl[2] ? MDR_q : 32'bz;  // Controlled_Buffer controlled_buffer_4
  assign MAddr = nor_1_out ? PC_q : 32'bz;  // Controlled_Buffer controlled_buffer_5
  nor nor_1 (nor_1_out, MControl[1], MControl[2]);
  Multiplexer #(.select(4), .width(32), .enable("false")) multiplexer_1 (
    .in1(MDR_q), .in2(PC_q), .in3(bit_extender_1_out), .in4(bit_extender_2_out), .in5(SP_q), .in6(LV_q),
    .in7(CPP_q), .in8(TOS_q), .in9(OPC_q), .out(B), .sel(RegOut));  // open: in0, in10, in11, in12, in13, in14, in15
  assign MEMIN = MEM;  // Buffer buffer_3, 32 bits wide

  // Other names for the same wires on the sheet: EnOutput[3:0] = RegOut; MBRIn[7:0] = MBR_IN; Ft = MControl[0];
  //   Re = MControl[1]; Wr = MControl[2]; MemAddr[31:0] = MAddr; MEMOUT[31:0] = MEM_2; MAR = RegIn[0]; MDR = RegIn[1];
  //   PC = RegIn[2]; SP = RegIn[3]; LV = RegIn[4]; CPP = RegIn[5]; TOS = RegIn[6]; OPC = RegIn[7]; H = RegIn[8]

  // Notes on the sheet:
  //   buffer_1 drives only 1 and floats otherwise
  //   buffer_2 drives only 1 and floats otherwise
endmodule

module Control (
  input  [7:0] MBR,
  input  Clk,
  input  [1:0] Flag_NZ,
  output [1:0] ALU_Sh,
  output [5:0] ALU_Control,
  output [8:0] C,
  output [2:0] M,
  output [3:0] B
);

  wire and_1_out, and_2_out, pull_resistor_1_node, pull_resistor_2_node;
  wire [1:0] register_1_q;
  wire [2:0] JMP;
  wire [7:0] and_3_out, and_4_out, bit_extender_1_out, or_3_out;
  wire [8:0] Addr, MPC_q, or_2_out;

  Pull_Resistor #(.pull(1)) pull_resistor_1 (.node(pull_resistor_1_node));
  Register #(.width(9)) MPC (.D(or_2_out), .en(pull_resistor_1_node), .Q(MPC_q), .clk(Clk));  // open: clr
  Register #(.width(2)) register_1 (.D(Flag_NZ), .en(pull_resistor_2_node), .Q(register_1_q), .clk(Clk));  // open: clr
  Pull_Resistor #(.pull(1)) pull_resistor_2 (.node(pull_resistor_2_node));
  or or_1 (or_2_out[8], and_1_out, and_2_out, Addr[8]);
  and and_1 (and_1_out, JMP[1], register_1_q[0]);
  and and_2 (and_2_out, JMP[0], register_1_q[1]);
  ROM #(.addrWidth(9), .dataWidth(12)) rom_1 (.addr(MPC_q), .data({Addr, JMP}));  // open: sel
  ROM #(.addrWidth(9), .dataWidth(24)) rom_2 (.addr(MPC_q), .data({ALU_Sh, ALU_Control, C, M, B}));  // open: sel
  assign or_2_out[7:0] = and_4_out | and_3_out;  // OR_Gate or_2, 8 bits wide
  assign and_3_out = bit_extender_1_out & or_3_out;  // AND_Gate and_3, 8 bits wide
  assign bit_extender_1_out = {{7{JMP[2]}}, JMP[2]};  // Bit_Extender bit_extender_1
  // Probe on Addr
  assign and_4_out = ~bit_extender_1_out & Addr[7:0];  // AND_Gate and_4, 8 bits wide
  assign or_3_out = Addr[7:0] | MBR;  // OR_Gate or_3, 8 bits wide
  // Probe on JMP

  // Notes on the sheet:
  //   contents of rom_1 (hex, n*v repeats v):
  //   4 0 18 20 0 30 38 0 48 50 0 60 68 0 978 0 88 90 0 a0 a8 b0 b8 c0 0 d0 d8 0 e8 f0 f8 100 0 110 118
  //   120 128 130 0 0 148 150 158 f0 168 170 178 118 188 190 198 f0 1a8 1b0 1b8 1c0 1c8 0 1d8 1e0 1e8 1f0
  //   1f8 0 208 210 218 27a 228 230 238 279 248 250 258 260 268 279 1d8 280 288 0 298 2a0 2a8 2b0 2b8 2c0
  //   2c8 2d0 2d8 2e0 2e8 2f0 2f8 300 308 310 318 320 328 330 338 0 348 350 358 360 368 370 378 0 380
  //   222*0 270
  //   contents of rom_2 (hex, n*v repeats v):
  //   350212 0 3604a5 148008 3c2141 3604a5 148008 3e2141 3604a5 148008 c2141 3604a5 148008 1c2141 350485 0
  //   3604a5 140202 142001 3600a5 140085 148041 140108 3600c5 182000 350485 350212 142144 148006 3c00a3
  //   350485 350252 142001 148006 3c0083 140148 3604a5 350212 142001 0 350212 948003 1c8003 3c00a6 350212
  //   948003 1c8003 3c0086 350212 948003 1c8003 3c00a7 148006 3c00a3 350212 148001 350212 3c0144 364002
  //   250212 948004 1c8003 3c0219 0 3604a5 144008 142001 140009 3604a5 144008 142001 140009 3604a5 360485
  //   148021 144008 142001 3f0009 374012 350202 350212 0 350212 48003 1c8003 3c00a7 354002 140211 350212
  //   948003 1c8003 350212 3e2005 352088 350212 948003 1c8003 3d0145 140481 140149 350485 140146 350212
  //   140808 1404a6 140202 1408a1 350086 140231 140085 140801 140148 191*0 140148
endmodule

module Timing (
  input  Clk,
  output out_2,
  output out_3,
  output out_4,
  output out_5,
  output out_6
);

  wire pull_resistor_1_node;
  wire [2:0] counter_1_q;

  Pull_Resistor #(.pull(1)) pull_resistor_1 (.node(pull_resistor_1_node));
  Decoder #(.select(3), .enable("false")) decoder_1 (
    .out0(out_2), .out1(out_3), .out2(out_4), .out3(out_5), .out4(out_6), .sel(counter_1_q));  // open: out5, out6, out7
  Counter #(.width(3), .max('h4)) counter_1 (
    .count(pull_resistor_1_node), .Q(counter_1_q), .clk(Clk));  // open: load, D, carry, clr
endmodule

module Test (
  input  [7:0] in_1
);

  wire clock_1_out;
  wire [7:0] ram_1_data, register_2_q;

  Register #(.trigger("falling")) register_1 (.D(ram_1_data), .clk(clock_1_out));  // open: en, Q, clr
  Register register_2 (.D(in_1), .Q(register_2_q), .clk(clock_1_out));  // open: en, clr
  Clock clock_1 (.out(clock_1_out));
  RAM ram_1 (.addr(register_2_q), .data(ram_1_data), .clk(clock_1_out));  // open: sel, ld, clr
endmodule
